# Fritzing sketch Day_16 (saved by Fritzing 1.0.2b)

parts:
  Part1 = Arduino Uno (Inventr.io)
  Grove1 = Grove 4 Digit Display

nets:
  N1: Part1.D5_PWM, Grove1.DIO
  N2: Part1.D6_PWM, Grove1.CLK
  5V: Part1.5V, Grove1.VCC
  GND: Part1.GND, Grove1.GND

custom parts:
  Arduino Uno (Inventr.io): The Arduino Uno is a microcontroller board based on the ATmega328 (datasheet). It has 14 digital input/output pins (of which 6 can be used as PWM outputs), 6 analog inputs, a 16 MHz ceramic resonator, a USB connection, a power jack, an ICSP header, and a reset button. It contains everything needed to support the microcontroller; simply connect it to a computer with a USB cable or power it with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
  Grove 4 Digit Display: A 4 7-seg display
