# Fritzing sketch Day_20 (saved by Fritzing 1.0.2b)
breadboards: 1

parts:
  Part1 = Arduino Uno (Inventr.io)
  Grove1 = Grove 4 Digit Display
  RE2 = KY-040 Rotary encoder [package=THT]
  Part2 = Passive Buzzer
  Generic_4x4_button_keypad1 = Generic 4x4 Keypad

nets:
  N1: Part1.A0, Generic_4x4_button_keypad1.C3
  N2: Part1.A1, Generic_4x4_button_keypad1.C4
  N3: Part1.D8, Generic_4x4_button_keypad1.R2
  N4: Part1.D9_PWM, Generic_4x4_button_keypad1.R3
  N5: Part1.D10_PWM/SS, Part2.S
  N6: Part1.D11_PWM/MOSI, Generic_4x4_button_keypad1.R4
  N7: Part1.D12/MISO, Part1.D7, Generic_4x4_button_keypad1.C1, Generic_4x4_button_keypad1.R1
  N8: Part1.D13/SCK, Generic_4x4_button_keypad1.C2
  GND: Part1.GND, Grove1.GND, RE2.GND, Part2.GND
  N9: Part1.D2, RE2.CLK
  N10: Part1.D3_PWM, RE2.DT
  N11: Part1.D5_PWM, Grove1.DIO
  N12: Part1.D6_PWM, Grove1.CLK
  VCC: Part1.5V, Grove1.VCC, RE2.Vcc

custom parts:
  Arduino Uno (Inventr.io): The Arduino Uno is a microcontroller board based on the ATmega328 (datasheet). It has 14 digital input/output pins (of which 6 can be used as PWM outputs), 6 analog inputs, a 16 MHz ceramic resonator, a USB connection, a power jack, an ICSP header, and a reset button. It contains everything needed to support the microcontroller; simply connect it to a computer with a USB cable or power it with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
  Grove 4 Digit Display: A 4 7-seg display
  KY-040 Rotary encoder: KY-040 Rotary Encoder with switch on breakout borad from AZ Delivery
  Generic 4x4 Keypad: generic 4x4 keypad 4 rows of four 6 mm tact switches cheap and nasty but works
