# Fritzing sketch Day_23 (saved by Fritzing 1.0.2b)
breadboards: 1

parts:
  Part1 = Arduino Uno (Inventr.io)
  OLED_I2C1 = OLED 128x64 I2C Monochrome Display
  Grove1 = Grove 4 Digit Display

nets:
  N1: Part1.A4/SDA, OLED_I2C1.SDA
  N2: Part1.A5/SCL, OLED_I2C1.SCK
  N3: Part1.D4, Grove1.DIO
  N4: Part1.D5_PWM, Grove1.CLK
  5V: Part1.5V, OLED_I2C1.VDD, Grove1.VCC
  GND: Part1.GND, OLED_I2C1.GND, Grove1.GND

custom parts:
  Arduino Uno (Inventr.io): The Arduino Uno is a microcontroller board based on the ATmega328 (datasheet). It has 14 digital input/output pins (of which 6 can be used as PWM outputs), 6 analog inputs, a 16 MHz ceramic resonator, a USB connection, a power jack, an ICSP header, and a reset button. It contains everything needed to support the microcontroller; simply connect it to a computer with a USB cable or power it with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
  Grove 4 Digit Display: A 4 7-seg display
