# Fritzing sketch Day_4 (saved by Fritzing 1.0.2b)
breadboards: 1

parts:
  LED1 = LED - 5mm [color="Red (633nm)" current=0.030A package="5 mm [THT]"]
  Part1 = Arduino Uno (Inventr.io)
  R1 = Resistor [tolerance=±5% power=0.25W resistance=220 package=THT]
  R2 = Resistor [tolerance=±5% power=0.25W resistance=10k package=THT]
  S1 = DIP Switch 3 Position
  R3 = Resistor [tolerance=±5% power=0.25W resistance=10k package=THT]
  R4 = Resistor [tolerance=±5% power=0.25W resistance=10k package=THT]
  R5 = Resistor [tolerance=±5% power=0.25W resistance=220 package=THT]
  R6 = Resistor [tolerance=±5% power=0.25W resistance=220 package=THT]
  LED2 = LED - 5mm [color="Blue (470nm)" current=0.030A package="5 mm [THT]"]
  LED3 = LED - 5mm [color="Green (560nm)" current=0.030A package="5 mm [THT]"]

nets:
  N1: LED1.cathode, Part1.GND, R2.Pin_1, R3.Pin_1, R4.Pin_1, LED2.cathode, LED3.cathode
  N2: LED1.anode, R1.Pin_0
  N3: Part1.D10_PWM/SS, R1.Pin_1
  N4: Part1.D11_PWM/MOSI, R6.Pin_1
  N5: Part1.D12/MISO, R5.Pin_1
  N6: Part1.D2, R2.Pin_0, S1.3
  N7: Part1.D3_PWM, S1.2, R3.Pin_0
  N8: Part1.D4, S1.1, R4.Pin_0
  N9: Part1.5V, S1.4, S1.5, S1.6
  N10: R5.Pin_0, LED3.anode
  N11: R6.Pin_0, LED2.anode

custom parts:
  Arduino Uno (Inventr.io): The Arduino Uno is a microcontroller board based on the ATmega328 (datasheet). It has 14 digital input/output pins (of which 6 can be used as PWM outputs), 6 analog inputs, a 16 MHz ceramic resonator, a USB connection, a power jack, an ICSP header, and a reset button. It contains everything needed to support the microcontroller; simply connect it to a computer with a USB cable or power it with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
