# Fritzing sketch Day_3 (saved by Fritzing 1.0.2b)
breadboards: 1

parts:
  Part1 = Arduino Uno (Inventr.io)
  LED1 = LED - 5mm [color="Blue (470nm)" current=0.030A package="5 mm [THT]"]
  R1 = Resistor [tolerance=±5% power=0.25W resistance=220 package=THT]
  LED2 = LED - 5mm [color="Green (555nm)" current=0.030A package="5 mm [THT]"]
  LED3 = LED - 5mm [color="Red (633nm)" current=0.030A package="5 mm [THT]"]
  R2 = Resistor [tolerance=±5% power=0.25W resistance=220 package=THT]
  R3 = Resistor [tolerance=±5% power=0.25W resistance=220 package=THT]

nets:
  N1: Part1.D8, LED3.anode
  N2: Part1.D9_PWM, LED2.anode
  N3: Part1.D10_PWM/SS, LED1.anode
  N4: Part1.GND, R1.Pin_0, R2.Pin_0, R3.Pin_0
  N5: LED1.cathode, R1.Pin_1
  N6: LED2.cathode, R2.Pin_1
  N7: LED3.cathode, R3.Pin_1

custom parts:
  Arduino Uno (Inventr.io): The Arduino Uno is a microcontroller board based on the ATmega328 (datasheet). It has 14 digital input/output pins (of which 6 can be used as PWM outputs), 6 analog inputs, a 16 MHz ceramic resonator, a USB connection, a power jack, an ICSP header, and a reset button. It contains everything needed to support the microcontroller; simply connect it to a computer with a USB cable or power it with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
