# Fritzing sketch Day_4 (saved by Fritzing 1.0.2b)
breadboards: 1

parts:
  Part1 = Arduino Uno (Inventr.io)
  LED1 = LED - 5mm [color="Red (633nm)" current=0.030A package="5 mm [THT]"]
  R1 = Resistor [tolerance=±5% power=0.25W resistance=220 package=THT]
  R2 = Resistor [tolerance=±5% power=0.25W resistance=10k package=THT]
  R3 = PHOTOCELL [package=photocell]

nets:
  N1: Part1.A0, R2.Pin_1, R3.P$1
  N2: Part1.D13/SCK, LED1.anode
  N3: Part1.GND, R1.Pin_0, R2.Pin_0
  N4: Part1.5V, R3.P$2
  N5: LED1.cathode, R1.Pin_1

custom parts:
  Arduino Uno (Inventr.io): The Arduino Uno is a microcontroller board based on the ATmega328 (datasheet). It has 14 digital input/output pins (of which 6 can be used as PWM outputs), 6 analog inputs, a 16 MHz ceramic resonator, a USB connection, a power jack, an ICSP header, and a reset button. It contains everything needed to support the microcontroller; simply connect it to a computer with a USB cable or power it with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
