# Fritzing sketch Day_5 (saved by Fritzing 1.0.2b)
breadboards: 1

parts:
  Part1 = Arduino Uno (Inventr.io)
  LED1 = LED - 5mm [color="Red (633nm)" current=0.030A package="5 mm [THT]"]
  R1 = Resistor [tolerance=±5% power=0.25W resistance=220 package=THT]
  S1 = DIP Switch 3 Position
  R2 = Resistor [tolerance=±5% power=0.25W resistance=10k package=THT]
  LED2 = LED - 5mm [color="Blue (430nm)" current=0.030A package="5 mm [THT]"]
  R3 = Resistor [tolerance=±5% power=0.25W resistance=220 package=THT]
  R4 = Resistor [tolerance=±5% power=0.25W resistance=10k package=THT]

nets:
  N1: Part1.D8, LED2.anode
  N2: Part1.D9_PWM, LED1.anode
  N3: Part1.GND, R1.Pin_0, R2.Pin_0, R3.Pin_0, R4.Pin_0
  N4: Part1.D2, S1.3, R4.Pin_1
  N5: Part1.D3_PWM, S1.1, R2.Pin_1
  N6: Part1.5V, S1.4, S1.6
  N7: LED1.cathode, R1.Pin_1
  N8: LED2.cathode, R3.Pin_1

custom parts:
  Arduino Uno (Inventr.io): The Arduino Uno is a microcontroller board based on the ATmega328 (datasheet). It has 14 digital input/output pins (of which 6 can be used as PWM outputs), 6 analog inputs, a 16 MHz ceramic resonator, a USB connection, a power jack, an ICSP header, and a reset button. It contains everything needed to support the microcontroller; simply connect it to a computer with a USB cable or power it with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
