# Fritzing sketch Day_12 (saved by Fritzing 1.0.2b)
breadboards: 1

parts:
  Part1 = Arduino Uno (Inventr.io)
  Generic_4x4_button_keypad1 = Generic 4x4 Keypad
  Part2 = Passive Buzzer

nets (from the breadboard view):
  N1: Part1.D8, Generic_4x4_button_keypad1.C3
  N2: Part1.D9_PWM, Generic_4x4_button_keypad1.C4
  N3: Part1.D10_PWM/SS, Part2.S
  N4: Part1.D2, Generic_4x4_button_keypad1.R4
  N5: Part1.D3_PWM, Generic_4x4_button_keypad1.R3
  N6: Part1.D4, Generic_4x4_button_keypad1.R2
  N7: Part1.D5_PWM, Generic_4x4_button_keypad1.R1
  N8: Part1.D6_PWM, Generic_4x4_button_keypad1.C1
  N9: Part1.D7, Generic_4x4_button_keypad1.C2
  GND: Part1.GND, Part2.GND

custom parts:
  Arduino Uno (Inventr.io): The Arduino Uno is a microcontroller board based on the ATmega328 (datasheet). It has 14 digital input/output pins (of which 6 can be used as PWM outputs), 6 analog inputs, a 16 MHz ceramic resonator, a USB connection, a power jack, an ICSP header, and a reset button. It contains everything needed to support the microcontroller; simply connect it to a computer with a USB cable or power it with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
  Generic 4x4 Keypad: generic 4x4 keypad 4 rows of four 6 mm tact switches cheap and nasty but works
