# Fritzing sketch Advanced_Day_2 (saved by Fritzing 1.0.2b)
breadboards: 1

parts:
  LED1 = LED - 5mm [color="Red (633nm)" current=0.030A package="5 mm [THT]"]
  Part1 = Arduino Uno (Inventr.io)
  R1 = Resistor [tolerance=±5% power=0.25W resistance=220 package=THT]
  SW1 = DIP SWITCH [package=dipswitch-02]
  R2 = Resistor [tolerance=±5% power=0.25W resistance=10k package=THT]

nets:
  N1: LED1.cathode, Part1.GND, R2.Pin_1
  N2: LED1.anode, R1.Pin_0
  N3: Part1.D12/MISO, R1.Pin_1
  N4: Part1.D2, SW1.1, SW1.2, R2.Pin_0
  N5: Part1.5V, SW1.3, SW1.4

custom parts:
  Arduino Uno (Inventr.io): The Arduino Uno is a microcontroller board based on the ATmega328 (datasheet). It has 14 digital input/output pins (of which 6 can be used as PWM outputs), 6 analog inputs, a 16 MHz ceramic resonator, a USB connection, a power jack, an ICSP header, and a reset button. It contains everything needed to support the microcontroller; simply connect it to a computer with a USB cable or power it with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
